// Digital circuit RISCV-pipeline.dig as structural Verilog
module RISCV_pipeline (
  input  [31:0] in_1,
  input  in_2,
  input  [31:0] in_3,
  input  [31:0] in_4,
  input  in_5
);

  wire and_1_out, and_2_out, u_comparator_result, u_HazardDetectionUnit_controlmux,
       u_HazardDetectionUnit_if_id_write, u_HazardDetectionUnit_pcwrite, u_MUX_2inputs_multOUT_output1,
       u_MUX_2inputs_multOUT_output2, u_MUX_2inputs_multOUT_output3, u_MUX_2inputs_multOUT_output4,
       u_MUX_2inputs_multOUT_output5, u_output_control_branch, u_output_control_memread,
       u_output_control_memtoreg, u_output_control_memwrite, u_output_control_regwrite,
       u_pipelineRegEXMEM_memreadout, u_pipelineRegEXMEM_memtoregout, u_pipelineRegEXMEM_memwriteout,
       u_pipelineRegEXMEM_regwriteout, u_pipelineRegIDEX_branchout, u_pipelineRegIDEX_eqout,
       u_pipelineRegIDEX_memreadout, u_pipelineRegIDEX_memtoregout, u_pipelineRegIDEX_memwriteout,
       u_pipelineRegIDEX_regwriteout, u_pipelineRegMEMWB_memtoregout, u_pipelineRegMEMWB_regwriteout;
  wire [1:0] u_Forwarding_forwarda, u_Forwarding_forwardb, u_MUX_2inputs_multOUT_output6,
       u_MUX_2inputs_multOUT_output7, u_MUX_2inputs_multOUT_output8, u_output_control_aluop,
       u_output_control_alusrca, u_output_control_alusrcb, u_pipelineRegIDEX_aluopout,
       u_pipelineRegIDEX_alusrcaout, u_pipelineRegIDEX_alusrcbout;
  wire [2:0] u_ALU_control_selector;
  wire [11:0] u_splitter_2_address_out, u_splitter_address_out;
  wire [31:0] Memory_2_d, Memory_d, u_Add_result, u_ALU_result, u_imm_gen_imm_out, u_MUX_2inputs_2_output,
       u_MUX_2inputs_3_output, u_MUX_2inputs_4_output, u_MUX_2inputs_output, u_MUX_3inputs_2_output,
       u_MUX_3inputs_output, u_PCAddress_result, u_pipelineReg_instructionoutput, u_pipelineReg_pcout,
       u_pipelineRegEXMEM_aluout, u_pipelineRegEXMEM_instructionoutput, u_pipelineRegEXMEM_op2out,
       u_pipelineRegIDEX_immout, u_pipelineRegIDEX_instructionoutput, u_pipelineRegIDEX_pcout,
       u_pipelineRegIDEX_rg1out, u_pipelineRegIDEX_rg2out, u_pipelineRegMEMWB_aluout,
       u_pipelineRegMEMWB_instructionoutput, u_pipelineRegMEMWB_meminstructionout, u_reg32_memoutput,
       u_register_block_rg1_data, u_register_block_rg2_data;

  MUX_2inputs #(.applicationType("GHDL")) u_MUX_2inputs (
    .enter1(u_Add_result), .enter2(u_PCAddress_result), .selector(and_1_out), .\output (u_MUX_2inputs_output));
  reg32 #(.applicationType("GHDL")) u_reg32 (
    .memData(u_MUX_2inputs_output), .PCWrite(u_HazardDetectionUnit_pcwrite), .CLK(in_2), .RESET(in_5),
    .memOutput(u_reg32_memoutput));
  Add #(.applicationType("GHDL")) u_Add (.A(u_reg32_memoutput), .B(in_1), .Result(u_Add_result));
  splitter #(.applicationType("GHDL")) u_splitter (
    .address_in(u_reg32_memoutput), .address_out(u_splitter_address_out));
  RAMDualPort #(.AddrBits(12), .isProgramMemory("true"), .Bits(32)) Memory (
    .A(u_splitter_address_out), .Din(in_3), .str(1'b0), .C(in_2), .ld(1'b1), .D(Memory_d));
  pipelineReg #(.applicationType("GHDL")) u_pipelineReg (
    .instruction(Memory_d), .PC(u_reg32_memoutput), .IFFlush(and_2_out),
    .IFIDWrite(u_HazardDetectionUnit_if_id_write), .CLK(in_2), .RESET(in_5),
    .instructionOutput(u_pipelineReg_instructionoutput), .PCOut(u_pipelineReg_pcout));
  output_control #(.applicationType("GHDL")) u_output_control (
    .instruction(u_pipelineReg_instructionoutput), .MemtoReg(u_output_control_memtoreg),
    .MemWrite(u_output_control_memwrite), .MemRead(u_output_control_memread),
    .Branch(u_output_control_branch), .ALUOp(u_output_control_aluop), .ALUSrcB(u_output_control_alusrcb),
    .ALUSrcA(u_output_control_alusrca), .RegWrite(u_output_control_regwrite));
  and and_1 (and_1_out, u_MUX_2inputs_multOUT_output5, u_comparator_result);
  register_block #(.applicationType("GHDL")) u_register_block (
    .instruction(u_pipelineReg_instructionoutput), .instruction2(u_pipelineRegMEMWB_instructionoutput),
    .CLK(in_2), .reg_write(u_pipelineRegMEMWB_regwriteout), .rgw_data(u_MUX_2inputs_4_output), .RESET(in_5),
    .rg1_data(u_register_block_rg1_data), .rg2_data(u_register_block_rg2_data));
  imm_gen #(.applicationType("GHDL")) u_imm_gen (
    .instruction(u_pipelineReg_instructionoutput), .imm_out(u_imm_gen_imm_out));
  PCAddress #(.applicationType("GHDL")) u_PCAddress (
    .A(u_pipelineReg_pcout), .B(u_imm_gen_imm_out), .C(u_register_block_rg1_data),
    .instruction(u_pipelineReg_instructionoutput), .Result(u_PCAddress_result));
  MUX_2inputs_multOUT #(.applicationType("GHDL")) u_MUX_2inputs_multOUT (
    .enter1(u_output_control_regwrite), .enter2(u_output_control_memtoreg),
    .enter3(u_output_control_memread), .enter4(u_output_control_memwrite), .enter5(u_output_control_branch),
    .enter6(u_output_control_aluop), .enter7(u_output_control_alusrcb), .enter8(u_output_control_alusrca),
    .selector(u_HazardDetectionUnit_controlmux), .output1(u_MUX_2inputs_multOUT_output1),
    .output2(u_MUX_2inputs_multOUT_output2), .output3(u_MUX_2inputs_multOUT_output3),
    .output4(u_MUX_2inputs_multOUT_output4), .output5(u_MUX_2inputs_multOUT_output5),
    .output6(u_MUX_2inputs_multOUT_output6), .output7(u_MUX_2inputs_multOUT_output7),
    .output8(u_MUX_2inputs_multOUT_output8));
  comparator #(.applicationType("GHDL")) u_comparator (
    .rg1(u_register_block_rg1_data), .rg2(u_register_block_rg2_data),
    .instruction(u_pipelineReg_instructionoutput), .result(u_comparator_result));
  and and_2 (and_2_out, u_pipelineRegIDEX_branchout, u_pipelineRegIDEX_eqout);
  pipelineRegIDEX #(.applicationType("GHDL")) u_pipelineRegIDEX (
    .instruction(u_pipelineReg_instructionoutput), .Imm(u_imm_gen_imm_out), .eq(u_comparator_result),
    .RegWrite(u_MUX_2inputs_multOUT_output1), .MemToReg(u_MUX_2inputs_multOUT_output2),
    .memRead(u_MUX_2inputs_multOUT_output3), .memWrite(u_MUX_2inputs_multOUT_output4),
    .Branch(u_MUX_2inputs_multOUT_output5), .ALUOp(u_MUX_2inputs_multOUT_output6),
    .ALUSrcB(u_MUX_2inputs_multOUT_output7), .Rg1(u_register_block_rg1_data),
    .Rg2(u_register_block_rg2_data), .CLK(in_2), .Flush(and_2_out), .PC(u_pipelineReg_pcout),
    .ALUSrcA(u_MUX_2inputs_multOUT_output8), .RESET(in_5),
    .instructionOutput(u_pipelineRegIDEX_instructionoutput), .ImmOut(u_pipelineRegIDEX_immout),
    .eqOut(u_pipelineRegIDEX_eqout), .RegWriteOut(u_pipelineRegIDEX_regwriteout),
    .MemToRegOut(u_pipelineRegIDEX_memtoregout), .memReadOut(u_pipelineRegIDEX_memreadout),
    .memWriteOut(u_pipelineRegIDEX_memwriteout), .BranchOut(u_pipelineRegIDEX_branchout),
    .ALUOpOUT(u_pipelineRegIDEX_aluopout), .ALUSrcBOUT(u_pipelineRegIDEX_alusrcbout),
    .Rg1Out(u_pipelineRegIDEX_rg1out), .Rg2Out(u_pipelineRegIDEX_rg2out), .PCOut(u_pipelineRegIDEX_pcout),
    .ALUSrcAOUT(u_pipelineRegIDEX_alusrcaout));
  Forwarding #(.applicationType("GHDL")) u_Forwarding (
    .IDEXInstruction(u_pipelineRegIDEX_instructionoutput),
    .EXMEMInstruction(u_pipelineRegEXMEM_instructionoutput), .EXMEMRegWrite(u_pipelineRegEXMEM_regwriteout),
    .MEMWBInstruction(u_pipelineRegMEMWB_instructionoutput), .MEMWBRegWrite(u_pipelineRegMEMWB_regwriteout),
    .ForwardA(u_Forwarding_forwarda), .ForwardB(u_Forwarding_forwardb));
  HazardDetectionUnit #(.applicationType("GHDL")) u_HazardDetectionUnit (
    .IF_ID_Instruction(u_pipelineReg_instructionoutput), .Branch_ID(u_output_control_branch),
    .ID_EX_MemRead(u_pipelineRegIDEX_memreadout), .ID_EX_RegWrite(u_pipelineRegIDEX_regwriteout),
    .ID_EX_Instruction(u_pipelineRegIDEX_instructionoutput), .EX_MEM_MemRead(u_pipelineRegEXMEM_memreadout),
    .EX_MEM_RegWrite(u_pipelineRegEXMEM_regwriteout),
    .EX_MEM_Instruction(u_pipelineRegEXMEM_instructionoutput), .PCWrite(u_HazardDetectionUnit_pcwrite),
    .IF_ID_Write(u_HazardDetectionUnit_if_id_write), .ControlMux(u_HazardDetectionUnit_controlmux));
  MUX_3inputs #(.applicationType("GHDL")) u_MUX_3inputs (
    .enter1(u_pipelineRegIDEX_rg1out), .enter2(u_MUX_2inputs_4_output), .enter3(u_pipelineRegEXMEM_aluout),
    .selector(u_Forwarding_forwarda), .\output (u_MUX_3inputs_output));
  MUX_3inputs #(.applicationType("GHDL")) u_MUX_3inputs_2 (
    .enter1(u_pipelineRegIDEX_rg2out), .enter2(u_MUX_2inputs_4_output), .enter3(u_pipelineRegEXMEM_aluout),
    .selector(u_Forwarding_forwardb), .\output (u_MUX_3inputs_2_output));
  MUX_2inputs #(.applicationType("GHDL")) u_MUX_2inputs_2 (
    .enter1(u_MUX_3inputs_2_output), .enter2(u_pipelineRegIDEX_immout),
    .selector(u_pipelineRegIDEX_alusrcbout), .\output (u_MUX_2inputs_2_output));
  ALU_control #(.applicationType("GHDL")) u_ALU_control (
    .instruction(u_pipelineRegIDEX_instructionoutput), .ALUOp(u_pipelineRegIDEX_aluopout),
    .selector(u_ALU_control_selector));
  MUX_2inputs #(.applicationType("GHDL")) u_MUX_2inputs_3 (
    .enter1(u_MUX_3inputs_output), .enter2(u_pipelineRegIDEX_pcout), .enter3(in_4),
    .selector(u_pipelineRegIDEX_alusrcaout), .\output (u_MUX_2inputs_3_output));
  ALU #(.applicationType("GHDL")) u_ALU (
    .A(u_MUX_2inputs_3_output), .B(u_MUX_2inputs_2_output), .selector(u_ALU_control_selector),
    .Result(u_ALU_result));
  pipelineRegEXMEM #(.applicationType("GHDL")) u_pipelineRegEXMEM (
    .instruction(u_pipelineRegIDEX_instructionoutput), .RegWrite(u_pipelineRegIDEX_regwriteout),
    .MemToReg(u_pipelineRegIDEX_memtoregout), .memRead(u_pipelineRegIDEX_memreadout),
    .memWrite(u_pipelineRegIDEX_memwriteout), .ALU(u_ALU_result), .Op2(u_MUX_3inputs_2_output), .CLK(in_2),
    .RESET(in_5), .instructionOutput(u_pipelineRegEXMEM_instructionoutput),
    .RegWriteOut(u_pipelineRegEXMEM_regwriteout), .MemToRegOut(u_pipelineRegEXMEM_memtoregout),
    .memReadOut(u_pipelineRegEXMEM_memreadout), .memWriteOut(u_pipelineRegEXMEM_memwriteout),
    .ALUOut(u_pipelineRegEXMEM_aluout), .Op2Out(u_pipelineRegEXMEM_op2out));
  splitter #(.applicationType("GHDL")) u_splitter_2 (
    .address_in(u_pipelineRegEXMEM_aluout), .address_out(u_splitter_2_address_out));
  RAMDualPort #(.AddrBits(12), .isProgramMemory("true"), .Bits(32)) Memory_2 (
    .A(u_splitter_2_address_out), .Din(u_pipelineRegEXMEM_op2out), .str(u_pipelineRegEXMEM_memwriteout),
    .C(in_2), .ld(u_pipelineRegEXMEM_memreadout), .D(Memory_2_d));
  pipelineRegMEMWB #(.applicationType("GHDL")) u_pipelineRegMEMWB (
    .instruction(u_pipelineRegEXMEM_instructionoutput), .MemInstruction(Memory_2_d),
    .RegWrite(u_pipelineRegEXMEM_regwriteout), .MemToReg(u_pipelineRegEXMEM_memtoregout),
    .ALU(u_pipelineRegEXMEM_aluout), .CLK(in_2), .RESET(in_5),
    .instructionOutput(u_pipelineRegMEMWB_instructionoutput),
    .MemInstructionOut(u_pipelineRegMEMWB_meminstructionout), .RegWriteOut(u_pipelineRegMEMWB_regwriteout),
    .MemToRegOut(u_pipelineRegMEMWB_memtoregout), .ALUOut(u_pipelineRegMEMWB_aluout));
  MUX_2inputs #(.applicationType("GHDL")) u_MUX_2inputs_4 (
    .enter1(u_pipelineRegMEMWB_aluout), .enter2(u_pipelineRegMEMWB_meminstructionout),
    .selector(u_pipelineRegMEMWB_memtoregout), .\output (u_MUX_2inputs_4_output));
endmodule

/* Code of MUX_2inputs:
LIBRARY ieee;
USE ieee.std_logic_1164.all;

ENTITY MUX_2inputs IS
	PORT(
		enter1, enter2 : IN STD_LOGIC_VECTOR (31 downto 0);
		selector : IN STD_LOGIC;
		output : OUT STD_LOGIC_VECTOR (31 downto 0)
	);
END MUX_2inputs;

ARCHITECTURE MUX_logic OF MUX_2inputs IS
	BEGIN
		output <= enter1 WHEN selector = '0' ELSE
			enter2;

	END MUX_logic;
--------------------------------------------------------------------------------
*/

/* Code of reg32:
LIBRARY ieee;
USE ieee.std_logic_1164.all;
USE ieee.numeric_std.all;

ENTITY reg32 IS
	PORT(
		memData : IN STD_LOGIC_VECTOR(31 downto 0);
		PCWrite : IN STD_LOGIC;
		CLK : IN STD_LOGIC;
		RESET : IN STD_LOGIC;
		memOutput : OUT STD_LOGIC_VECTOR(31 downto 0)
	);
END reg32;

ARCHITECTURE reg32_logic OF reg32 IS
	BEGIN
	
		PROCESS(CLK, RESET)
			BEGIN
				IF(Reset = '1') THEN
					memOutput <= x"00000000";
				ELSIF (RISING_EDGE(CLK) AND (PCWrite = '1')) THEN
					memOutput <= memData;
				ELSE
					memOutput <= memOutput;
				END IF;
		END PROCESS;

	END reg32_logic;
*/

/* Code of Add:
LIBRARY ieee;
USE ieee.std_logic_1164.all;
USE ieee.numeric_std.all;

ENTITY Add IS
	PORT(
		A, B: IN STD_LOGIC_VECTOR(31 downto 0);
		Result : OUT STD_LOGIC_VECTOR(31 downto 0)
	);
END Add;

ARCHITECTURE Add_logic OF Add IS
	BEGIN
    		Result <= std_logic_vector(unsigned(A) + unsigned(B));

	END Add_logic;
*/

/* Code of splitter:
LIBRARY ieee;
USE ieee.std_logic_1164.all;

ENTITY splitter IS
	PORT(
		address_in : IN  STD_LOGIC_VECTOR(31 downto 0);
		address_out : OUT STD_LOGIC_VECTOR(11 downto 0)
	);
END splitter;

ARCHITECTURE behavioral OF splitter IS
BEGIN
	address_out <= address_in(13 downto 2);
END behavioral;
*/

/* Code of pipelineReg:
LIBRARY ieee;
USE ieee.std_logic_1164.all;
USE ieee.numeric_std.all;

ENTITY pipelineReg IS
	PORT(
		instruction : IN STD_LOGIC_VECTOR(31 downto 0);
		PC : IN STD_LOGIC_VECTOR(31 downto 0);
		IFFlush : IN STD_LOGIC;
		IFIDWrite : IN STD_LOGIC;
		CLK : IN STD_LOGIC;
		RESET : IN STD_LOGIC;
		instructionOutput : OUT STD_LOGIC_VECTOR(31 downto 0);
		PCOut : OUT STD_LOGIC_VECTOR(31 downto 0)
	);
END pipelineReg;

ARCHITECTURE pipelineReg_logic OF pipelineReg IS
	BEGIN
	
		PROCESS(CLK, RESET)
			BEGIN
				IF(Reset = '1') THEN
					PCOut <= x"00000000";
					instructionOutput <= x"00000000";
				ELSIF(IFFlush = '1') THEN
						instructionOutput <= "00000000000000000000000000010011";
						PCOut <= PCOut;
				ELSIF RISING_EDGE(CLK) THEN
					IF IFIDWrite = '1' THEN
						instructionOutput <= instruction;
						PCOut <= PC;
					ELSE
						instructionOutput <= instructionOutput;
						PCOut <= PCOut;
					END IF;
				ELSE
					instructionOutput <= instructionOutput;
					PCOut <= PCOut;
				END IF;
		END PROCESS;

	END pipelineReg_logic;
*/

/* Code of output_control:
LIBRARY ieee;
USE ieee.std_logic_1164.all;
USE ieee.numeric_std.all;

ENTITY output_control IS
	PORT(
		instruction : IN STD_LOGIC_VECTOR(31 downto 0);
		MemtoReg : OUT STD_LOGIC;
		MemWrite : OUT STD_LOGIC;
		MemRead : OUT STD_LOGIC;
		Branch : OUT STD_LOGIC;
		ALUOp : OUT STD_LOGIC_VECTOR (1 downto 0);
		ALUSrcB : OUT STD_LOGIC_VECTOR (1 downto 0);
		ALUSrcA : OUT STD_LOGIC_VECTOR (1 downto 0);
		RegWrite : OUT STD_LOGIC
	);
END output_control;

ARCHITECTURE output_control_logic OF output_control IS

	CONSTANT opAritmetica : STD_LOGIC_VECTOR(6 downto 0) := "0110011";
	CONSTANT LW : STD_LOGIC_VECTOR(6 downto 0) := "0000011";
	CONSTANT SW : STD_LOGIC_VECTOR(6 downto 0) := "0100011";
	CONSTANT beq : STD_LOGIC_VECTOR(6 downto 0) := "1100011";
	CONSTANT arit_im : STD_LOGIC_VECTOR(6 downto 0) := "0010011";
	CONSTANT auipc : STD_LOGIC_VECTOR(6 downto 0) := "0010111";
	CONSTANT lui : STD_LOGIC_VECTOR(6 downto 0) := "0110111";
	CONSTANT jal : STD_LOGIC_VECTOR(6 downto 0) := "1101111";
	CONSTANT jalr : STD_LOGIC_VECTOR(6 downto 0) := "1100111";
	SIGNAL opcode : STD_LOGIC_VECTOR(6 downto 0);

	BEGIN
		opcode <= instruction(6 downto 0);
		PROCESS(opcode, instruction)
		BEGIN
		CASE Opcode IS
            		WHEN opAritmetica =>
                		ALUSrcB <= "00"; ALUSrcA <= "00"; ALUOp <= "10"; MemRead <= '0'; MemWrite <= '0'; Branch <= '0'; RegWrite <= '1'; MemtoReg <= '0';

            		WHEN LW =>
                		ALUSrcB <= "01"; ALUSrcA <= "00"; ALUOp <= "00"; MemRead <= '1'; MemWrite <= '0'; Branch <= '0'; RegWrite <= '1'; MemtoReg <= '1';

            		WHEN SW =>
                		ALUSrcB <= "01"; ALUSrcA <= "00"; ALUOp <= "00"; MemRead <= '0'; MemWrite <= '1'; Branch <= '0'; RegWrite <= '0'; MemtoReg <= '0';

            		WHEN beq =>
                		ALUSrcB <= "00"; ALUSrcA <= "00"; ALUOp <= "01"; MemRead <= '0'; MemWrite <= '0'; Branch <= '1'; RegWrite <= '0'; MemtoReg <= '0';

			WHEN arit_im =>
				IF(instruction /= x"00000013") THEN
					ALUSrcB <= "01"; ALUSrcA <= "00"; ALUOp <= "10"; MemRead <= '0'; MemWrite <= '0'; Branch <= '0'; RegWrite <= '1'; MemtoReg <= '0';
				ELSE
					ALUSrcB <= "00"; ALUSrcA <= "00"; ALUOp <= "00"; MemRead <= '0'; MemWrite <= '0'; Branch <= '0'; RegWrite <= '0'; MemtoReg <= '0';
				END IF;
			WHEN auipc =>
				ALUSrcB <= "01"; ALUSrcA <= "01"; ALUOp <= "00"; MemRead <= '0'; MemWrite <= '0'; Branch <= '0'; RegWrite <= '1'; MemtoReg <= '0';
			WHEN lui =>
				ALUSrcB <= "01"; ALUSrcA <= "10"; ALUOp <= "00"; MemRead <= '0'; MemWrite <= '0'; Branch <= '0'; RegWrite <= '1'; MemtoReg <= '0';
			WHEN jal | jalr =>
				ALUSrcB <= "10"; ALUSrcA <= "01"; ALUOp <= "00"; MemRead <= '0'; MemWrite <= '0'; Branch <= '1'; RegWrite <= '1'; MemtoReg <= '0';
            		WHEN OTHERS =>
                		ALUSrcB <= "00"; ALUSrcA <= "00"; ALUOp <= "00"; MemRead <= '0'; MemWrite <= '0'; Branch <= '0'; RegWrite <= '0'; MemtoReg <= '0';
        		END CASE;
    		END PROCESS;
	END output_control_logic;
*/

/* Code of register_block:
LIBRARY ieee;
USE ieee.std_logic_1164.all;
USE ieee.numeric_std.all;

ENTITY register_block IS
	PORT(
		instruction  : IN  STD_LOGIC_VECTOR(31 downto 0); -- Instrução no estágio ID
		instruction2 : IN  STD_LOGIC_VECTOR(31 downto 0); -- Instrução no estágio WB
		CLK          : IN  STD_LOGIC;
		reg_write    : IN  STD_LOGIC;
		rgw_data     : IN  STD_LOGIC_VECTOR(31 downto 0);
		RESET : IN STD_LOGIC;
		rg1_data     : OUT STD_LOGIC_VECTOR(31 downto 0);
		rg2_data     : OUT STD_LOGIC_VECTOR(31 downto 0)
	);
END register_block;

ARCHITECTURE register_logic OF register_block IS

	type reg_array is array (0 to 31) of std_logic_vector(31 downto 0);
	signal registers : reg_array := (others => (others => '0'));
	signal rg1, rg2, rgw : STD_LOGIC_VECTOR(4 downto 0);

BEGIN
	-- Extração direta dos índices dos registradores
	rg1 <= instruction(19 downto 15);
	rg2 <= instruction(24 downto 20);
	rgw <= instruction2(11 downto 7);

	------------------------------------------------------------------
	-- 1. ESCRITA SÍNCRONA (Acontece APENAS na borda de subida do CLK)
	------------------------------------------------------------------
	PROCESS(CLK, RESET)
	BEGIN
		IF(Reset = '1') THEN
			registers <= (others => (others => '0'));
		ELSIF RISING_EDGE(CLK) THEN
			IF (reg_write = '1' AND rgw /= "00000") THEN
				registers(to_integer(unsigned(rgw))) <= rgw_data;
			END IF;
		END IF;
	END PROCESS;

	------------------------------------------------------------------
	-- 2. LEITURA COMBINACIONAL COM BYPASS (Responde INSTANTANEAMENTE)
	------------------------------------------------------------------
	-- Leitura da porta 1 (rg1):
	rg1_data <= (others => '0') WHEN (rg1 = "00000") ELSE
	            rgw_data       WHEN (reg_write = '1' AND rgw /= "00000" AND rgw = rg1) ELSE
	            registers(to_integer(unsigned(rg1)));

	-- Leitura da porta 2 (rg2):
	rg2_data <= (others => '0') WHEN (rg2 = "00000") ELSE
	            rgw_data       WHEN (reg_write = '1' AND rgw /= "00000" AND rgw = rg2) ELSE
	            registers(to_integer(unsigned(rg2)));

END register_logic;
*/

/* Code of imm_gen:
LIBRARY ieee;
USE ieee.std_logic_1164.all;

ENTITY imm_gen IS
	PORT(
		instruction : IN  STD_LOGIC_VECTOR(31 downto 0);
		imm_out     : OUT STD_LOGIC_VECTOR(31 downto 0)
	);
END imm_gen;

ARCHITECTURE behavioral OF imm_gen IS
	ALIAS opcode : STD_LOGIC_VECTOR(6 downto 0) IS instruction(6 downto 0);
BEGIN

	PROCESS(instruction, opcode)
	BEGIN
		CASE opcode IS
			-- Tipo-I (ex: Load, addi)
			WHEN "0000011" | "0010011" | "1100111" =>
				imm_out <= (31 downto 12 => instruction(31)) & instruction(31 downto 20);

			-- Tipo-S (ex: Store)
			WHEN "0100011" =>
				imm_out <= (31 downto 12 => instruction(31)) & instruction(31 downto 25) & instruction(11 downto 7);

			-- Tipo-B (ex: Branch / Desvios)
			WHEN "1100011" =>
				imm_out <= (31 downto 12 => instruction(31)) & instruction(7) & instruction(30 downto 25) & instruction(11 downto 8) & '0';
				
			-- Tipo-U
			WHEN "0010111" | "0110111"  =>
				imm_out <= instruction(31 downto 12) & x"000";
			-- Tipo-J
			WHEN "1101111" =>
    				imm_out <= (31 downto 21 => instruction(31)) &  -- 11 bits de extensão de sinal
               			instruction(31)                  &  -- imm[20]       (1 bit)
               			instruction(19 downto 12)        &  -- imm[19:12]    (8 bits)
               			instruction(20)                  &  -- imm[11]       (1 bit)
               			instruction(30 downto 21)        &  -- imm[10:1]     (10 bits)
               		'0';
			WHEN OTHERS =>
				imm_out <= (others => '0');
		END CASE;
	END PROCESS;

END behavioral;
*/

/* Code of PCAddress:
LIBRARY ieee;
USE ieee.std_logic_1164.all;
USE ieee.numeric_std.all;

ENTITY PCAddress IS
	PORT(
		A, B, C: IN STD_LOGIC_VECTOR(31 downto 0);
		instruction : IN STD_LOGIC_VECTOR(31 downto 0);
		Result : OUT STD_LOGIC_VECTOR(31 downto 0)
	);
END PCAddress;

ARCHITECTURE PCAddress_logic OF PCAddress IS
	BEGIN
		
    		Result <= std_logic_vector(unsigned(C) + unsigned(B)) WHEN 
			(instruction(6 downto 0) = "1100111") ELSE
			std_logic_vector(unsigned(A) + unsigned(B));

	END PCAddress_logic;
*/

/* Code of MUX_2inputs_multOUT:
LIBRARY ieee;
USE ieee.std_logic_1164.all;

ENTITY MUX_2inputs_multOUT IS
	PORT(
		enter1, enter2, enter3, 
		enter4 , enter5 : IN STD_LOGIC;
		enter6 : IN STD_LOGIC_VECTOR (1 downto 0);
		enter7  : IN STD_LOGIC_VECTOR (1 downto 0);
		enter8  : IN STD_LOGIC_VECTOR (1 downto 0);
		selector : IN STD_LOGIC;
		output1, output2, output3,
		output4, output5 : OUT STD_LOGIC;
		output6 : OUT STD_LOGIC_VECTOR (1 downto 0);
		output7 : OUT STD_LOGIC_VECTOR (1 downto 0);
		output8 : OUT STD_LOGIC_VECTOR (1 downto 0)
	);
END MUX_2inputs_multOUT;

ARCHITECTURE MUX_logic OF MUX_2inputs_multOUT IS
	BEGIN
		output1 <= '0' WHEN selector = '1' ELSE
			enter1;
		output2 <= '0' WHEN selector = '1' ELSE
			enter2;
		output3 <= '0' WHEN selector = '1' ELSE
			enter3;
		output4 <= '0' WHEN selector = '1' ELSE
			enter4;
		output5 <= '0' WHEN selector = '1' ELSE
			enter5;
		output6 <= "00" WHEN selector = '1' ELSE
			enter6;
		output7 <= "00" WHEN selector = '1' ELSE
			enter7;
		output8 <= "00" WHEN selector = '1' ELSE
			enter8;

	END MUX_logic;
--------------------------------------------------------------------------------
*/

/* Code of comparator:
LIBRARY ieee;
USE ieee.std_logic_1164.all;

ENTITY comparator IS
	PORT(
		rg1 : IN  STD_LOGIC_VECTOR(31 downto 0);
		rg2 : IN  STD_LOGIC_VECTOR(31 downto 0);
		instruction : IN  STD_LOGIC_VECTOR(31 downto 0);
		result : OUT STD_LOGIC
	);
END comparator;

ARCHITECTURE behavioral OF comparator IS
	SIGNAL funct3 : STD_LOGIC_VECTOR(2 downto 0);
	SIGNAL opcode : STD_LOGIC_VECTOR(6 downto 0);
BEGIN
	opcode <= instruction(6 downto 0);
	funct3 <= instruction(14 downto 12);
	result <= '1' WHEN (((opcode = "1100011") AND ((rg1 = rg2 AND funct3 = "000") OR (rg1 /= rg2 AND funct3 = "001"))) OR
			(opcode = "1101111") OR (opcode = "1100111")) ELSE
		'0';
END behavioral;
*/

/* Code of pipelineRegIDEX:
LIBRARY ieee;
USE ieee.std_logic_1164.all;
USE ieee.numeric_std.all;

ENTITY pipelineRegIDEX IS
	PORT(
		instruction : IN STD_LOGIC_VECTOR(31 downto 0);
		Imm : IN STD_LOGIC_VECTOR(31 downto 0);
		eq: IN STD_LOGIC;
		RegWrite : IN STD_LOGIC;
		MemToReg : IN STD_LOGIC;

		memRead : IN STD_LOGIC;
		memWrite : IN STD_LOGIC;
		Branch : IN STD_LOGIC;

		ALUOp : IN STD_LOGIC_VECTOR (1 downto 0);
		ALUSrcB : IN STD_LOGIC_VECTOR (1 downto 0);

		Rg1 : IN STD_LOGIC_VECTOR(31 downto 0);
		Rg2 : IN STD_LOGIC_VECTOR(31 downto 0);
		CLK : IN STD_LOGIC;
		Flush : IN STD_LOGIC;
		PC : IN STD_LOGIC_VECTOR(31 downto 0);
		ALUSrcA : IN STD_LOGIC_VECTOR(1 downto 0);
		RESET : IN STD_LOGIC;
		instructionOutput : OUT STD_LOGIC_VECTOR(31 downto 0);
		ImmOut : OUT STD_LOGIC_VECTOR(31 downto 0);
		eqOut: OUT STD_LOGIC;
		
		RegWriteOut : OUT STD_LOGIC;
		MemToRegOut : OUT STD_LOGIC;
		
		memReadOut : OUT STD_LOGIC;
		memWriteOut : OUT STD_LOGIC;
		BranchOut : OUT STD_LOGIC;

		ALUOpOUT : OUT STD_LOGIC_VECTOR (1 downto 0);
		ALUSrcBOUT : OUT STD_LOGIC_VECTOR(1 downto 0);

		Rg1Out : OUT STD_LOGIC_VECTOR(31 downto 0);
		Rg2Out : OUT STD_LOGIC_VECTOR(31 downto 0);
		PCOut : OUT STD_LOGIC_VECTOR(31 downto 0);
		ALUSrcAOUT : OUT STD_LOGIC_VECTOR(1 downto 0)
	);
END pipelineRegIDEX;

ARCHITECTURE pipelineRegIDEX_logic OF pipelineRegIDEX IS
	SIGNAL opcode : STD_LOGIC_VECTOR(6 downto 0);
	BEGIN
		opcode <= instruction(6 downto 0);
		PROCESS(CLK, RESET)
			BEGIN
				IF((Flush = '1') OR (RESET = '1')) THEN
					IF RESET = '1' THEN
						instructionOutput <= X"00000000";
						BranchOut <= '0';
						AluOpOut <= "00";
						AluSrcBOut <= "00";
						AluSrcAOut <= "00";
						ImmOut <= X"00000000";
						Rg1Out <= X"00000000";
						Rg2Out <= X"00000000";
						PCOut <= X"00000000";
					ELSE
						instructionOutput <= instructionOutput;
						BranchOut <= BranchOut;
						AluOpOut <= AluOpOut;
						AluSrcBOut <= AluSrcBOut;
						AluSrcAOut <= AluSrcAOut;
						ImmOut <= ImmOut;
						Rg1Out <= Rg1Out;
						Rg2Out <= Rg2Out;
						PCOut <= PCOut;
						IF(opcode = "1101111") THEN
							RegWriteOut <= RegWrite;
						ELSE
							RegWriteOut <= '0';
						END IF;
					END IF;

					memToRegOut <= '0';
					MemWriteOut <= '0';
					MemReadOut <= '0';
					eqOut <= '0';

				ELSIF RISING_EDGE(CLK) THEN
					instructionOutput <= instruction;

					RegWriteOut <= RegWrite;
					memToRegOut <= memToReg;

					BranchOut <= Branch;
					MemWriteOut <= MemWrite;
					MemReadOut <= MemRead;
					
					AluOpOut <= AluOp;
					AluSrcBOut <= AluSrcB;
					AluSrcAOut <= AluSrcA;

					Rg1Out <= Rg1;
					Rg2Out <= Rg2;
					PCOut <= PC;
					eqOut <= eq;
					ImmOut <= Imm;
				ELSE
					instructionOutput <= instructionOutput;
					RegWriteOut <= RegWriteOut;
					memToRegOut <= memToRegOut;

					BranchOut <= BranchOut;
					MemWriteOut <= MemWriteOut;
					MemReadOut <= MemReadOut;
					
					AluOpOut <= AluOpOut;
					AluSrcBOut <= AluSrcBOut;
					AluSrcAOut <= AluSrcAOut;
					ImmOut <= ImmOut;
					Rg1Out <= Rg1Out;
					Rg2Out <= Rg2Out;
					PCOut <= PCOut;
					eqOut <= eqOut;
					ImmOut <= ImmOut;
				END IF;
		END PROCESS;

	END pipelineRegIDEX_logic;
*/

/* Code of Forwarding:
LIBRARY ieee;
USE ieee.std_logic_1164.all;

ENTITY Forwarding IS
	PORT(
		IDEXInstruction : IN STD_LOGIC_VECTOR(31 downto 0);
		EXMEMInstruction : IN STD_LOGIC_VECTOR(31 downto 0);
		EXMEMRegWrite : IN STD_LOGIC;
		MEMWBInstruction : IN STD_LOGIC_VECTOR(31 downto 0);
		MEMWBRegWrite : IN STD_LOGIC;
		ForwardA : OUT STD_LOGIC_VECTOR(1 downto 0);
		ForwardB : OUT STD_LOGIC_VECTOR(1 downto 0)
	);
END Forwarding;

ARCHITECTURE behavioral OF Forwarding IS
	SIGNAL Rs1 : STD_LOGIC_VECTOR(4 downto 0);
	SIGNAL Rs2 : STD_LOGIC_VECTOR(4 downto 0);
	SIGNAL RdMEMWB : STD_LOGIC_VECTOR(4 downto 0);
	SIGNAL RdEXMEM : STD_LOGIC_VECTOR(4 downto 0);
BEGIN
	Rs1 <= IDEXInstruction(19 downto 15);
	Rs2 <= IDEXInstruction(24 downto 20);
	RdMEMWB <= MEMWBInstruction(11 downto 7);
	RdEXMEM <= EXMEMInstruction(11 downto 7);

	PROCESS(Rs1,
    Rs2,
    RdMEMWB,
    RdEXMEM,
    EXMEMRegWrite,
    MEMWBRegWrite)
	BEGIN
		IF (EXMEMRegWrite = '1') AND (RdEXMEM /= "00000") AND (RdEXMEM = Rs1) THEN
    			ForwardA <= "10";
		ELSIF (MEMWBRegWrite = '1') AND (RdMEMWB /= "00000") 
   		AND NOT (EXMEMRegWrite = '1' AND RdEXMEM /= "00000" AND RdEXMEM = Rs1)
   		AND (RdMEMWB = Rs1) THEN
    			ForwardA <= "01";
		ELSE
			ForwardA <= "00";
		END IF;

		IF (EXMEMRegWrite = '1') AND (RdEXMEM /= "00000") AND (RdEXMEM = Rs2) THEN
    			ForwardB <= "10";
		ELSIF (MEMWBRegWrite = '1') AND (RdMEMWB /= "00000") 
   		AND NOT (EXMEMRegWrite = '1' AND RdEXMEM /= "00000" AND RdEXMEM = Rs2)
   		AND (RdMEMWB = Rs2) THEN
    			ForwardB <= "01";
		ELSE
			ForwardB <= "00";
		END IF;
		
	END PROCESS;
END behavioral;
*/

/* Code of HazardDetectionUnit:
LIBRARY ieee;
USE ieee.std_logic_1164.all;
USE ieee.numeric_std.all;

ENTITY HazardDetectionUnit IS
	PORT(
		IF_ID_Instruction : IN STD_LOGIC_VECTOR(31 downto 0);
		
		Branch_ID         : IN STD_LOGIC;
		
		ID_EX_MemRead     : IN STD_LOGIC;
		ID_EX_RegWrite    : IN STD_LOGIC;
		ID_EX_Instruction  : IN STD_LOGIC_VECTOR(31 downto 0);

		EX_MEM_MemRead     : IN STD_LOGIC;
		EX_MEM_RegWrite    : IN STD_LOGIC;
		EX_MEM_Instruction  : IN STD_LOGIC_VECTOR(31 downto 0);
		
		PCWrite           : OUT STD_LOGIC;
		IF_ID_Write       : OUT STD_LOGIC;
		ControlMux        : OUT STD_LOGIC
	);
END HazardDetectionUnit;

ARCHITECTURE behavioral OF HazardDetectionUnit IS
	SIGNAL ID_EX_RegisterRd : STD_LOGIC_VECTOR(4 downto 0);
	SIGNAL EX_MEM_RegisterRd : STD_LOGIC_VECTOR(4 downto 0);
	SIGNAL IF_ID_Rs1 : STD_LOGIC_VECTOR(4 downto 0);
	SIGNAL IF_ID_Rs2 : STD_LOGIC_VECTOR(4 downto 0);
	SIGNAL IF_ID_opcode : STD_LOGIC_VECTOR(6 downto 0);
BEGIN
	ID_EX_RegisterRd <= ID_EX_Instruction(11 downto 7);
	EX_MEM_RegisterRd <= EX_MEM_Instruction(11 downto 7);
	IF_ID_Rs1 <= IF_ID_Instruction(19 downto 15);
	IF_ID_Rs2 <= IF_ID_Instruction(24 downto 20);
	IF_ID_opcode <= IF_ID_Instruction(6 downto 0);
	
	PROCESS(IF_ID_Rs1, IF_ID_Rs2, Branch_ID,
	        ID_EX_MemRead, ID_EX_RegWrite, ID_EX_RegisterRd, EX_MEM_RegWrite, EX_MEM_RegisterRd)
		
		VARIABLE stall_load_use : BOOLEAN;
		VARIABLE stall_branch   : BOOLEAN;
		
	BEGIN
		stall_load_use := ((ID_EX_MemRead = '1') AND 
		                  (ID_EX_RegisterRd /= "00000") AND 
		                  ((ID_EX_RegisterRd = IF_ID_Rs1) OR (ID_EX_RegisterRd = IF_ID_Rs2)));

		stall_branch := ((Branch_ID = '1') AND 
			((ID_EX_RegWrite = '1') AND (ID_EX_RegisterRd /= "00000") AND 
			 ((ID_EX_RegisterRd = IF_ID_Rs1) OR (ID_EX_RegisterRd = IF_ID_Rs2))))
			OR 
			((Branch_ID = '1') AND
			((EX_MEM_RegWrite = '1') AND (EX_MEM_RegisterRd /= "00000") AND 
			 ((EX_MEM_RegisterRd = IF_ID_Rs1) OR (EX_MEM_RegisterRd = IF_ID_Rs2))));

		IF IF_ID_opcode = "1101111" THEN
			PCWrite     <= '1';
			IF_ID_Write <= '0';
			ControlMux  <= '0'; 
		ELSIF stall_load_use OR stall_branch THEN
			PCWrite     <= '0'; -- Congela o Program Counter (PC)
			IF_ID_Write <= '0'; -- Congela o Registrador IF/ID
			ControlMux  <= '1'; -- Injeta Bolha/NOP no registrador ID/EX
		ELSE
			PCWrite     <= '1'; -- Fluxo normal de execução
			IF_ID_Write <= '1';
			ControlMux  <= '0';
		END IF;
		
	END PROCESS;
END behavioral;
*/

/* Code of MUX_3inputs:
LIBRARY ieee;
USE ieee.std_logic_1164.all;

ENTITY MUX_3inputs IS
	PORT(
		enter1, enter2, enter3 : IN STD_LOGIC_VECTOR (31 downto 0);
		selector: IN STD_LOGIC_VECTOR (1 downto 0);
		output : OUT STD_LOGIC_VECTOR (31 downto 0)
	);
END MUX_3inputs;

ARCHITECTURE MUX_logic OF MUX_3inputs IS
	BEGIN
		output <= enter1 WHEN selector = "00" ELSE
			enter2 WHEN selector = "01" ELSE
			enter3;

	END MUX_logic;
--------------------------------------------------------------------------------
*/

/* Code of MUX_2inputs:
LIBRARY ieee;
USE ieee.std_logic_1164.all;

ENTITY MUX_2inputs IS
	PORT(
		enter1, enter2 : IN STD_LOGIC_VECTOR (31 downto 0);
		selector : IN STD_LOGIC_VECTOR(1 downto 0);
		output : OUT STD_LOGIC_VECTOR (31 downto 0)
	);
END MUX_2inputs;

ARCHITECTURE MUX_logic OF MUX_2inputs IS
	BEGIN
		output <= enter1 WHEN selector = "00" ELSE
			enter2 WHEN selector = "01" ELSE
			"00000000000000000000000000000100";

	END MUX_logic;
--------------------------------------------------------------------------------
*/

/* Code of ALU_control:
LIBRARY ieee;
USE ieee.std_logic_1164.all;

ENTITY ALU_control IS
	PORT(
		instruction : IN  STD_LOGIC_VECTOR(31 downto 0);
		ALUOp  : IN STD_LOGIC_VECTOR(1 downto 0);
		selector : OUT STD_LOGIC_VECTOR(2 downto 0)
	);
END ALU_control;

ARCHITECTURE behavioral OF ALU_control IS
	SIGNAL opcode : STD_LOGIC_VECTOR(6 downto 0);
	SIGNAL funct3 : STD_LOGIC_VECTOR(14 downto 12);
	SIGNAL funct7 : STD_LOGIC_VECTOR(31 downto 25);
BEGIN

	opcode <= instruction(6 downto 0);
	funct3 <= instruction(14 downto 12);
	funct7 <= instruction(31 downto 25);

	PROCESS(ALUOp, opcode, funct3, funct7)
		BEGIN
			selector <= "000";
			IF(ALUOp = "00" OR opcode = "0000011" OR opcode = "0100011") THEN
				selector <= "000";
			ELSIF(ALUOp = "01" OR opcode = "1100011") THEN
				selector <= "001";
			ELSE
				IF(opcode = "0110011" OR opcode = "0010011") THEN
					IF(funct7 = "0000000" OR opcode = "0010011") THEN
						IF(funct3 = "000") THEN
							selector <= "000";
						ELSIF(funct3 = "111") THEN
							selector <= "010";
						ELSIF(funct3 = "110") THEN
							selector <= "011";
						ELSIF(funct3 = "100") THEN
							selector <= "100";
						ELSIF(funct3 = "001") THEN
							selector <= "101";
						ELSIF(funct3 = "101") THEN
							selector <= "110";
						END IF;
					ELSIF(funct7 = "0100000") THEN
						selector <= "001";
					END IF;
				ELSIF(opcode = "0010111") THEN
					selector <= "111";
				END IF;
			END IF;
		END PROCESS;
END behavioral;
*/

/* Code of MUX_2inputs:
LIBRARY ieee;
USE ieee.std_logic_1164.all;

ENTITY MUX_2inputs IS
	PORT(
		enter1, enter2, enter3 : IN STD_LOGIC_VECTOR (31 downto 0);
		selector : IN STD_LOGIC_VECTOR (1 downto 0);
		output : OUT STD_LOGIC_VECTOR (31 downto 0)
	);
END MUX_2inputs;

ARCHITECTURE MUX_logic OF MUX_2inputs IS
	BEGIN
		output <= enter1 WHEN selector = "00" ELSE
			enter2 WHEN selector = "01" ELSE
			enter3;

	END MUX_logic;
--------------------------------------------------------------------------------
*/

/* Code of ALU:
LIBRARY ieee;
USE ieee.std_logic_1164.all;
USE ieee.numeric_std.all;

ENTITY ALU IS
	PORT(
		A, B : IN STD_LOGIC_VECTOR(31 downto 0);
		selector : IN STD_LOGIC_VECTOR(2 downto 0);
		Result : OUT STD_LOGIC_VECTOR(31 downto 0)
	);
END ALU;

ARCHITECTURE ALU_logic OF ALU IS

	signal B_eff    : STD_LOGIC_VECTOR(31 downto 0);

	constant allZero : std_logic_vector(31 downto 0) := (others => '0');
	constant allOne : std_logic_vector(31 downto 0) := (others => '1');

    	signal Sum_ext  : UNSIGNED(32 downto 0);

    	signal Res_temp : STD_LOGIC_VECTOR(31 downto 0);
	signal and_temp : STD_LOGIC_VECTOR(31 downto 0);
	signal or_temp : STD_LOGIC_VECTOR(31 downto 0);
	signal xor_temp : STD_LOGIC_VECTOR(31 downto 0);
	signal sll_temp : STD_LOGIC_VECTOR(31 downto 0);
	signal srl_temp : STD_LOGIC_VECTOR(31 downto 0);

    	signal Cin_vec  : UNSIGNED(32 downto 0);

	BEGIN
		and_temp <= A AND B;
		or_temp <= A OR B;
		xor_temp <= A XOR B;
		sll_temp <= std_logic_vector(shift_left(unsigned(A), to_integer(unsigned(B))));
		srl_temp <= std_logic_vector(shift_right(unsigned(A), to_integer(unsigned(B))));

------------------------------------

    B_eff <= (B xor allOne) WHEN (selector = "01") ELSE
		B;

    Cin_vec <= unsigned(allZero & selector(0));

    Sum_ext <= unsigned('0' & A) + unsigned('0' & B_eff) + Cin_vec;

    Res_temp <= std_logic_vector(Sum_ext(31 downto 0));

    Result <= and_temp WHEN (selector = "010") ELSE
		or_temp WHEN (selector = "011") ELSE
		xor_temp WHEN (selector = "100") ELSE
		sll_temp WHEN (selector = "101") ELSE
		srl_temp WHEN (selector = "110") ELSE
		Res_temp;

	END ALU_logic;
*/

/* Code of pipelineRegEXMEM:
LIBRARY ieee;
USE ieee.std_logic_1164.all;
USE ieee.numeric_std.all;

ENTITY pipelineRegEXMEM IS
	PORT(
		instruction : IN STD_LOGIC_VECTOR(31 downto 0);

		RegWrite : IN STD_LOGIC;
		MemToReg : IN STD_LOGIC;

		memRead : IN STD_LOGIC;
		memWrite : IN STD_LOGIC;

		ALU : IN STD_LOGIC_VECTOR(31 downto 0);
		Op2 : IN STD_LOGIC_VECTOR(31 downto 0);
		CLK : IN STD_LOGIC;
		RESET : IN STD_LOGIC;

		instructionOutput : OUT STD_LOGIC_VECTOR(31 downto 0);
		
		RegWriteOut : OUT STD_LOGIC;
		MemToRegOut : OUT STD_LOGIC;
		
		memReadOut : OUT STD_LOGIC;
		memWriteOut : OUT STD_LOGIC;
	
		ALUOut : OUT STD_LOGIC_VECTOR(31 downto 0);
		Op2Out : OUT STD_LOGIC_VECTOR(31 downto 0)
	);
END pipelineRegEXMEM;

ARCHITECTURE pipelineRegMEMWB_logic OF pipelineRegEXMEM IS
	BEGIN
	
		PROCESS(CLK, RESET)
			BEGIN
				IF RESET = '1' THEN
					instructionOutput <= X"00000000";
					RegWriteOut <= '0';
					memToRegOut <= '0';
					MemWriteOut <= '0';
					MemReadOut <= '0';
					ALUOut <= X"00000000";
					Op2Out <= X"00000000";
				ELSIF RISING_EDGE(CLK) THEN
					instructionOutput <= instruction;

					RegWriteOut <= RegWrite;
					memToRegOut <= memToReg;

					MemWriteOut <= MemWrite;
					MemReadOut <= MemRead;
					ALUOut <= ALU;
					Op2Out <= Op2;
					
				ELSE
					instructionOutput <= instructionOutput;
					RegWriteOut <= RegWriteOut;
					memToRegOut <= memToRegOut;

					MemWriteOut <= MemWriteOut;
					MemReadOut <= MemReadOut;
					ALUOut <= ALUOut;
					Op2Out <= Op2Out;
					
				END IF;
		END PROCESS;

	END pipelineRegMEMWB_logic;
*/

/* Code of pipelineRegMEMWB:
LIBRARY ieee;
USE ieee.std_logic_1164.all;
USE ieee.numeric_std.all;

ENTITY pipelineRegMEMWB IS
	PORT(
		instruction : IN STD_LOGIC_VECTOR(31 downto 0);
		MemInstruction : IN STD_LOGIC_VECTOR(31 downto 0);

		RegWrite : IN STD_LOGIC;
		MemToReg : IN STD_LOGIC;

		ALU : IN STD_LOGIC_VECTOR(31 downto 0);
		CLK : IN STD_LOGIC;
		RESET : IN STD_LOGIC;

		instructionOutput : OUT STD_LOGIC_VECTOR(31 downto 0);
		MemInstructionOut : OUT STD_LOGIC_VECTOR(31 downto 0);
		
		RegWriteOut : OUT STD_LOGIC;
		MemToRegOut : OUT STD_LOGIC;
	
		ALUOut : OUT STD_LOGIC_VECTOR(31 downto 0)
	);
END pipelineRegMEMWB;

ARCHITECTURE pipelineRegMEMWB_logic OF pipelineRegMEMWB IS
	BEGIN
	
		PROCESS(CLK, RESET)
			BEGIN
				IF RESET = '1' THEN
					instructionOutput <= X"00000000";
					MeminstructionOut <= X"00000000";
					RegWriteOut <= '0';
					memToRegOut <= '0';
					ALUOut <= X"00000000";
				ELSIF RISING_EDGE(CLK) THEN
					instructionOutput <= instruction;
					MeminstructionOut <= Meminstruction;

					RegWriteOut <= RegWrite;
					memToRegOut <= memToReg;

					ALUOut <= ALU;
					
				ELSE
					instructionOutput <= instructionOutput;
					MeminstructionOut <= MeminstructionOut;
					RegWriteOut <= RegWriteOut;
					memToRegOut <= memToRegOut;

					ALUOut <= ALUOut;
					
				END IF;
		END PROCESS;

	END pipelineRegMEMWB_logic;
*/
