// Digital circuit RISCV.dig as structural Verilog
module RISCV (
  input  [31:0] in_1,
  input  in_2,
  input  in_3
);

  wire and_1_out, or_1_out, u_ALU_zero, u_output_control_iord, u_output_control_irwrite,
       u_output_control_memread, u_output_control_memtoreg, u_output_control_memwrite,
       u_output_control_pcsource, u_output_control_pcwrite, u_output_control_pcwritecond,
       u_output_control_regwrite;
  wire [1:0] u_ALU_control_selector, u_output_control_aluop, u_output_control_alusrca,
       u_output_control_alusrcb;
  wire [11:0] u_splitter_address_out;
  wire [31:0] Memory_d, u_ALU_result, u_imm_gen_imm_out, u_IR_block_instruction, u_MUX_2inputs_2_output,
       u_MUX_2inputs_3_output, u_MUX_2inputs_output, u_MUX_3inputs_2_output, u_MUX_3inputs_output,
       u_reg32_2_memoutput, u_reg32_3_memoutput, u_reg32_4_memoutput, u_reg32_5_memoutput,
       u_reg32_6_memoutput, u_reg32_memoutput, u_register_block_rg1_data, u_register_block_rg2_data;

  reg32 #(.applicationType("GHDL")) u_reg32 (
    .memData(u_MUX_2inputs_3_output), .PCWrite(or_1_out), .CLK(in_2), .memOutput(u_reg32_memoutput));
  splitter #(.applicationType("GHDL")) u_splitter (
    .address_in(u_MUX_2inputs_output), .address_out(u_splitter_address_out));
  MUX_2inputs #(.applicationType("GHDL")) u_MUX_2inputs (
    .enter1(u_reg32_memoutput), .enter2(u_reg32_6_memoutput), .selector(u_output_control_iord),
    .\output (u_MUX_2inputs_output));
  RAMDualPort #(.AddrBits(12), .isProgramMemory("true"), .Bits(32)) Memory (
    .A(u_splitter_address_out), .Din(u_reg32_5_memoutput), .str(u_output_control_memwrite), .C(in_2),
    .ld(u_output_control_memread), .D(Memory_d));
  reg32 #(.applicationType("GHDL")) u_reg32_2 (.memData(Memory_d), .CLK(in_2), .memOutput(u_reg32_2_memoutput));
  reg32 #(.applicationType("GHDL")) u_reg32_3 (
    .memData(u_MUX_2inputs_output), .CLK(in_2), .memOutput(u_reg32_3_memoutput));
  IR_block #(.applicationType("GHDL")) u_IR_block (
    .memData(Memory_d), .CLK(in_2), .IRWrite(u_output_control_irwrite), .instruction(u_IR_block_instruction));
  MUX_2inputs #(.applicationType("GHDL")) u_MUX_2inputs_2 (
    .enter1(u_reg32_6_memoutput), .enter2(u_reg32_2_memoutput), .selector(u_output_control_memtoreg),
    .\output (u_MUX_2inputs_2_output));
  output_control #(.applicationType("GHDL")) u_output_control (
    .instruction(u_IR_block_instruction), .CLK(in_2), .RST(in_3), .IRWrite(u_output_control_irwrite),
    .MemtoReg(u_output_control_memtoreg), .MemWrite(u_output_control_memwrite),
    .MemRead(u_output_control_memread), .IorD(u_output_control_iord), .PCWrite(u_output_control_pcwrite),
    .PCWriteCond(u_output_control_pcwritecond), .PCSource(u_output_control_pcsource),
    .ALUOp(u_output_control_aluop), .ALUSrcB(u_output_control_alusrcb), .ALUSrcA(u_output_control_alusrca),
    .RegWrite(u_output_control_regwrite));
  register_block #(.applicationType("GHDL")) u_register_block (
    .instruction(u_IR_block_instruction), .CLK(in_2), .reg_write(u_output_control_regwrite),
    .rgw_data(u_MUX_2inputs_2_output), .rg1_data(u_register_block_rg1_data),
    .rg2_data(u_register_block_rg2_data));
  imm_gen #(.applicationType("GHDL")) u_imm_gen (.instruction(u_IR_block_instruction), .imm_out(u_imm_gen_imm_out));
  reg32 #(.applicationType("GHDL")) u_reg32_4 (
    .memData(u_register_block_rg1_data), .CLK(in_2), .memOutput(u_reg32_4_memoutput));
  reg32 #(.applicationType("GHDL")) u_reg32_5 (
    .memData(u_register_block_rg2_data), .CLK(in_2), .memOutput(u_reg32_5_memoutput));
  and and_1 (and_1_out, u_output_control_pcwritecond, u_ALU_zero);
  MUX_3inputs #(.applicationType("GHDL")) u_MUX_3inputs (
    .enter1(u_reg32_memoutput), .enter2(u_reg32_4_memoutput), .enter3(u_reg32_3_memoutput),
    .selector(u_output_control_alusrca), .\output (u_MUX_3inputs_output));
  MUX_3inputs #(.applicationType("GHDL")) u_MUX_3inputs_2 (
    .enter1(u_reg32_5_memoutput), .enter2(in_1), .enter3(u_imm_gen_imm_out),
    .selector(u_output_control_alusrcb), .\output (u_MUX_3inputs_2_output));
  or or_1 (or_1_out, u_output_control_pcwrite, and_1_out);
  ALU #(.applicationType("GHDL")) u_ALU (
    .A(u_MUX_3inputs_output), .B(u_MUX_3inputs_2_output), .selector(u_ALU_control_selector),
    .Zero(u_ALU_zero), .Result(u_ALU_result));
  ALU_control #(.applicationType("GHDL")) u_ALU_control (
    .instruction(u_IR_block_instruction), .ALUOp(u_output_control_aluop), .selector(u_ALU_control_selector));
  reg32 #(.applicationType("GHDL")) u_reg32_6 (.memData(u_ALU_result), .CLK(in_2), .memOutput(u_reg32_6_memoutput));
  MUX_2inputs #(.applicationType("GHDL")) u_MUX_2inputs_3 (
    .enter1(u_ALU_result), .enter2(u_reg32_6_memoutput), .selector(u_output_control_pcsource),
    .\output (u_MUX_2inputs_3_output));
endmodule

/* Code of reg32:
LIBRARY ieee;
USE ieee.std_logic_1164.all;
USE ieee.numeric_std.all;

ENTITY reg32 IS
	PORT(
		memData : IN STD_LOGIC_VECTOR(31 downto 0);
		PCWrite : IN STD_LOGIC;
		CLK : IN STD_LOGIC;
		memOutput : OUT STD_LOGIC_VECTOR(31 downto 0)
	);
END reg32;

ARCHITECTURE reg32_logic OF reg32 IS
	BEGIN
	
		PROCESS(CLK)
			BEGIN
				IF ((RISING_EDGE(CLK)) AND (PCWrite = '1')) THEN
					memOutput <= memData;
				ELSE
					memOutput <= memOutput;
				END IF;
		END PROCESS;

	END reg32_logic;
*/

/* Code of splitter:
LIBRARY ieee;
USE ieee.std_logic_1164.all;

ENTITY splitter IS
	PORT(
		address_in : IN  STD_LOGIC_VECTOR(31 downto 0);
		address_out : OUT STD_LOGIC_VECTOR(11 downto 0)
	);
END splitter;

ARCHITECTURE behavioral OF splitter IS
BEGIN
	address_out <= address_in(13 downto 2);
END behavioral;
*/

/* Code of MUX_2inputs:
LIBRARY ieee;
USE ieee.std_logic_1164.all;

ENTITY MUX_2inputs IS
	PORT(
		enter1, enter2 : IN STD_LOGIC_VECTOR (31 downto 0);
		selector : IN STD_LOGIC;
		output : OUT STD_LOGIC_VECTOR (31 downto 0)
	);
END MUX_2inputs;

ARCHITECTURE MUX_logic OF MUX_2inputs IS
	BEGIN
		output <= enter1 WHEN selector = '0' ELSE
			enter2;

	END MUX_logic;
--------------------------------------------------------------------------------
*/

/* Code of reg32:
LIBRARY ieee;
USE ieee.std_logic_1164.all;
USE ieee.numeric_std.all;

ENTITY reg32 IS
	PORT(
		memData : IN STD_LOGIC_VECTOR(31 downto 0);
		CLK : IN STD_LOGIC;
		memOutput : OUT STD_LOGIC_VECTOR(31 downto 0)
	);
END reg32;

ARCHITECTURE reg32_logic OF reg32 IS
	BEGIN
	
		PROCESS(CLK)
			BEGIN
				IF (RISING_EDGE(CLK)) THEN
					memOutput <= memData;
				ELSE
					memOutput <= memOutput;
				END IF;
		END PROCESS;

	END reg32_logic;
*/

/* Code of IR_block:
LIBRARY ieee;
USE ieee.std_logic_1164.all;
USE ieee.numeric_std.all;

ENTITY IR_block IS
	PORT(
		memData : IN STD_LOGIC_VECTOR(31 downto 0);
		CLK : IN STD_LOGIC;
		IRWrite : IN STD_LOGIC;
		instruction : OUT STD_LOGIC_VECTOR(31 downto 0)
	);
END IR_block;

ARCHITECTURE IR_logic OF IR_block IS
	BEGIN
	
		PROCESS(CLK)
			BEGIN
				IF (RISING_EDGE(CLK) AND IRWrite = '1') THEN
					instruction <= memData;
				ELSE
					instruction <= instruction;
				END IF;
		END PROCESS;

	END IR_logic;
*/

/* Code of output_control:
LIBRARY ieee;
USE ieee.std_logic_1164.all;
USE ieee.numeric_std.all;

ENTITY output_control IS
	PORT(
		instruction : IN STD_LOGIC_VECTOR(31 downto 0);
		CLK : IN STD_LOGIC;
		RST : IN STD_LOGIC;
		IRWrite : OUT STD_LOGIC;
		MemtoReg : OUT STD_LOGIC;
		MemWrite : OUT STD_LOGIC;
		MemRead : OUT STD_LOGIC;
		IorD : OUT STD_LOGIC;
		PCWrite : OUT STD_LOGIC;
		PCWriteCond : OUT STD_LOGIC;
		PCSource : OUT STD_LOGIC;
		ALUOp : OUT STD_LOGIC_VECTOR (1 downto 0);
		ALUSrcB : OUT STD_LOGIC_VECTOR (1 downto 0);
		ALUSrcA : OUT STD_LOGIC_VECTOR (1 downto 0);
		RegWrite : OUT STD_LOGIC
	);
END output_control;

ARCHITECTURE output_control_logic OF output_control IS

	CONSTANT opAritmetica : STD_LOGIC_VECTOR(6 downto 0) := "0110011";
	CONSTANT LW : STD_LOGIC_VECTOR(6 downto 0) := "0000011";
	CONSTANT SW : STD_LOGIC_VECTOR(6 downto 0) := "0100011";
	CONSTANT BRANCH : STD_LOGIC_VECTOR(6 downto 0) := "1100011";
	SIGNAL opcode : STD_LOGIC_VECTOR(6 downto 0);

	TYPE state_type IS (s_fetch, s_decode, s_addressComp, s_MemoryAccessLoad, s_MemoryAccessStore, s_MemoryReadLoad, 
	s_Execution, s_RtypeComp, s_Branch);
	SIGNAL state_next : state_type;
	SIGNAL state_reg : state_type := s_fetch;

	BEGIN

	opcode <= instruction(6 downto 0);
	PROCESS(clk)
		BEGIN
			IF RST = '1' THEN
				state_reg <= s_fetch;
			ELSIF rising_edge(CLK) THEN
				state_reg <= state_next;
			END IF;
		END PROCESS;

	PROCESS(state_reg, opcode)
		BEGIN
			CASE state_reg IS
				WHEN s_fetch =>
					state_next <= s_decode;

				WHEN s_decode =>
					IF opcode = LW OR opcode = SW THEN
						state_next <= s_addressComp;
					ELSIF opcode = opAritmetica THEN
						state_next <= s_Execution;
					ELSIF opcode = BRANCH THEN
						state_next <= s_Branch;
					ELSE
						state_next <= s_fetch; -- Opcode desconhecido reinicia a busca
					END IF;

				WHEN s_addressComp =>
					IF opcode = LW THEN
						state_next <= s_MemoryAccessLoad;
					ELSIF opcode = SW THEN
						state_next <= s_MemoryAccessStore;
					ELSE
						state_next <= s_fetch;
					END IF;

				WHEN s_MemoryAccessLoad =>
					state_next <= s_MemoryReadLoad;

				WHEN s_MemoryReadLoad | s_MemoryAccessStore | s_RtypeComp | s_Branch =>
					state_next <= s_fetch;

				WHEN s_Execution =>
					state_next <= s_RtypeComp;

				WHEN OTHERS =>
					state_next <= s_fetch;
			END CASE;
		END PROCESS;
				

		PROCESS(state_reg)
		BEGIN
			IRWrite     <= '0';
			MemtoReg    <= '0';
			MemWrite    <= '0';
			MemRead     <= '0';
			IorD        <= '0';
			PCWrite     <= '0';
			PCWriteCond <= '0';
			PCSource    <= '0';
			ALUOp       <= "00";
			ALUSrcB     <= "00";
			ALUSrcA     <= "00";
			RegWrite    <= '0';
			CASE state_reg IS
				WHEN s_fetch =>
					MemRead <= '1';
					ALUSrcA <= "00";
					IorD <= '0';
					IRWrite <= '1';
					ALUSrcB <= "01";
					ALUOp <= "00";
					PCWrite <= '1';
					PCSource <= '0';
				WHEN s_decode =>
					ALUSrcA <= "10";
					ALUSrcB <= "10";
					ALUOp <= "00";
				WHEN s_addressComp =>
					ALUSrcA <= "01";
					ALUSrcB <= "10";
					ALUOp <= "00";
				WHEN s_MemoryAccessLoad =>
					MemRead <= '1';
					IorD <= '1';
				WHEN s_MemoryReadLoad =>
					RegWrite <= '1';
					MemtoReg <= '1';
				WHEN s_MemoryAccessStore =>
					MemWrite <= '1';
					IorD <= '1';
				WHEN s_Execution =>
					ALUSrcA <= "01";
					ALUSrcB <= "00";
					ALUOp <= "10";
				WHEN s_RtypeComp =>
					RegWrite <= '1';
					MemtoReg <= '0';
				WHEN s_Branch =>
					ALUSrcA <= "01";
					ALUSrcB <= "00";
					ALUOp <= "01";
					PCWriteCond <= '1';
					PCSource <= '1';
				END CASE;
			END PROCESS;
	END output_control_logic;
*/

/* Code of register_block:
LIBRARY ieee;
USE ieee.std_logic_1164.all;
USE ieee.numeric_std.all;

ENTITY register_block IS
	PORT(
		instruction : IN STD_LOGIC_VECTOR(31 downto 0);
		CLK : IN STD_LOGIC;
		reg_write : IN STD_LOGIC;
		rgw_data : IN STD_LOGIC_VECTOR(31 downto 0);
		rg1_data , rg2_data : OUT STD_LOGIC_VECTOR(31 downto 0)
	);
END register_block;

ARCHITECTURE register_logic OF register_block IS

	type reg_array is array (0 to 31) of std_logic_vector(31 downto 0);
	signal registers : reg_array := (others => (others => '0'));
	signal value1 : STD_LOGIC_VECTOR(31 downto 0);
	signal value2 : STD_LOGIC_VECTOR(31 downto 0);
	signal rg1, rg2, rgw : STD_LOGIC_VECTOR(4 downto 0);

	BEGIN
		rg1 <= instruction(19 downto 15);
		rg2 <= instruction(24 downto 20);
		rgw <= instruction(11 downto 7);
		PROCESS(CLK)
			BEGIN
				IF (RISING_EDGE(CLK)) THEN
					IF (reg_write = '1' AND rgw /= "00000") THEN
						registers(to_integer(unsigned(rgw))) <= rgw_data;
					END IF;
				END IF;
		END PROCESS;

		rg1_data <= registers(to_integer(unsigned(rg1)));
		rg2_data <= registers(to_integer(unsigned(rg2)));

	END register_logic;
*/

/* Code of imm_gen:
LIBRARY ieee;
USE ieee.std_logic_1164.all;

ENTITY imm_gen IS
	PORT(
		instruction : IN  STD_LOGIC_VECTOR(31 downto 0);
		imm_out     : OUT STD_LOGIC_VECTOR(31 downto 0)
	);
END imm_gen;

ARCHITECTURE behavioral OF imm_gen IS
	ALIAS opcode : STD_LOGIC_VECTOR(6 downto 0) IS instruction(6 downto 0);
BEGIN

	PROCESS(instruction, opcode)
	BEGIN
		CASE opcode IS
			-- Tipo-I (ex: Load, addi)
			WHEN "0000011" | "0010011" =>
				imm_out <= (31 downto 12 => instruction(31)) & instruction(31 downto 20);

			-- Tipo-S (ex: Store)
			WHEN "0100011" =>
				imm_out <= (31 downto 12 => instruction(31)) & instruction(31 downto 25) & instruction(11 downto 7);

			-- Tipo-B (ex: Branch / Desvios)
			WHEN "1100011" =>
				imm_out <= (31 downto 12 => instruction(31)) & instruction(7) & instruction(30 downto 25) & instruction(11 downto 8) & '0';

			-- Padrão caso não utilize imediato
			WHEN OTHERS =>
				imm_out <= (others => '0');
		END CASE;
	END PROCESS;

END behavioral;
*/

/* Code of MUX_3inputs:
LIBRARY ieee;
USE ieee.std_logic_1164.all;

ENTITY MUX_3inputs IS
	PORT(
		enter1, enter2, enter3 : IN STD_LOGIC_VECTOR (31 downto 0);
		selector: IN STD_LOGIC_VECTOR (1 downto 0);
		output : OUT STD_LOGIC_VECTOR (31 downto 0)
	);
END MUX_3inputs;

ARCHITECTURE MUX_logic OF MUX_3inputs IS
	BEGIN
		output <= enter1 WHEN selector = "00" ELSE
			enter2 WHEN selector = "01" ELSE
			enter3;

	END MUX_logic;
--------------------------------------------------------------------------------
*/

/* Code of ALU:
LIBRARY ieee;
USE ieee.std_logic_1164.all;
USE ieee.numeric_std.all;

ENTITY ALU IS
	PORT(
		A, B : IN STD_LOGIC_VECTOR(31 downto 0);
		selector : IN STD_LOGIC_VECTOR(1 downto 0);
        	Zero    : OUT STD_LOGIC;
		Result : OUT STD_LOGIC_VECTOR(31 downto 0)
	);
END ALU;

ARCHITECTURE ALU_logic OF ALU IS

	signal B_eff    : STD_LOGIC_VECTOR(31 downto 0);

	constant allZero : std_logic_vector(31 downto 0) := (others => '0');
	constant allOne : std_logic_vector(31 downto 0) := (others => '1');

    	signal Sum_ext  : UNSIGNED(32 downto 0);

    	signal Res_temp : STD_LOGIC_VECTOR(31 downto 0);
	signal and_temp : STD_LOGIC_VECTOR(31 downto 0);
	signal or_temp : STD_LOGIC_VECTOR(31 downto 0);

    	signal Cin_vec  : UNSIGNED(32 downto 0);

	BEGIN

		and_temp <= A AND B;
		or_temp <= A OR B;

------------------------------------

    B_eff <= (B xor allOne) WHEN (selector = "01") ELSE
		B;

    Cin_vec <= unsigned(allZero & selector(0));

    Sum_ext <= unsigned('0' & A) + unsigned('0' & B_eff) + Cin_vec;

    Res_temp <= std_logic_vector(Sum_ext(31 downto 0));

    Zero <= '1' WHEN ((Res_temp = allZero) AND (selector(1) = '0')) ELSE
		'0';

    Result <= and_temp WHEN (selector = "10") ELSE
		or_temp WHEN (selector = "11") ELSE
		Res_temp;

	END ALU_logic;
*/

/* Code of ALU_control:
LIBRARY ieee;
USE ieee.std_logic_1164.all;

ENTITY ALU_control IS
	PORT(
		instruction : IN  STD_LOGIC_VECTOR(31 downto 0);
		ALUOp  : IN STD_LOGIC_VECTOR(1 downto 0);
		selector : OUT STD_LOGIC_VECTOR(1 downto 0)
	);
END ALU_control;

ARCHITECTURE behavioral OF ALU_control IS
	SIGNAL opcode : STD_LOGIC_VECTOR(6 downto 0);
	SIGNAL funct3 : STD_LOGIC_VECTOR(14 downto 12);
	SIGNAL funct7 : STD_LOGIC_VECTOR(31 downto 25);
BEGIN

	opcode <= instruction(6 downto 0);
	funct3 <= instruction(14 downto 12);
	funct7 <= instruction(31 downto 25);

	PROCESS(ALUOp, opcode, funct3, funct7)
		BEGIN
			selector <= "00";
			IF(ALUOp = "00" OR opcode = "0000011" OR opcode = "0100011") THEN
				selector <= "00";
			ELSIF(ALUOp = "01" OR opcode = "1100011") THEN
				selector <= "01";
			ELSE
				IF(opcode = "0110011") THEN
					IF(funct7 = "0000000") THEN
						IF(funct3 = "000") THEN
							selector <= "00";
						ELSIF(funct3 = "111") THEN
							selector <= "10";
						ELSIF(funct3 = "110") THEN
							selector <= "11";
						END IF;
					ELSIF(funct7 = "0100000") THEN
						selector <= "01";
					END IF;
				END IF;
			END IF;
		END PROCESS;
END behavioral;
*/
